# Fritzing sketch TSFRL_master_module (saved by Fritzing 0.9.0b)
circuit board: 9cm x 7cm
perfboards: 1

parts:
  KEYS_pins = rounded female pin header, 8 pins [form="♀ (female rounded)"]
  IC2 = Hex Inverter Schmitt Trigger SN74HC14 [package="DIP (Dual Inline)"]
  DATA/POWER_pins = male pin header, 5 pins [form="♂ (male)"]
  TEST = LED - 3mm [color="Blue (525nm)" current=20pA package="3 mm [THT]"]
  DATA = LED - 3mm [color="Yellow (595nm)" package="3 mm [THT]"]
  ERROR = LED - 3mm [color="Red (633nm)" package="3 mm [THT]"]
  DONE = LED - 3mm [color="Green (570nm)" package="3 mm [THT]"]
  ARDUINO_NANO = Arduino Nano (Rev3.0)
  R2 = Resistor [tolerance=±5% resistance=220 package=THT]
  R3 = Resistor [tolerance=±5% resistance=220 package=THT]
  R4 = Resistor [tolerance=±5% resistance=220 package=THT]
  R5 = Resistor [tolerance=±5% resistance=220 package=THT]
  U2 = DS75176BN [package=dil08]
  LCD_pins = male pin header, 4 pins [form="♂ (male)"]

nets:
  GND: KEYS_pins.pin1, IC2.GND, DATA/POWER_pins.pin1, TEST.cathode, DATA.cathode, ERROR.cathode, DONE.cathode, ARDUINO_NANO.GND, U2.GND, LCD_pins.pin4
  N1: KEYS_pins.pin2, DATA/POWER_pins.pin5, ARDUINO_NANO.RESET
  N2: KEYS_pins.pin3, IC2.3A
  N3: KEYS_pins.pin4, IC2.2A
  N4: KEYS_pins.pin5, IC2.1A
  N5: KEYS_pins.pin6, IC2.4A
  N6: KEYS_pins.pin7, IC2.5A
  5V: KEYS_pins.pin8, IC2.VCC, DATA/POWER_pins.pin4, ARDUINO_NANO.5V, U2.VCC, LCD_pins.pin3
  N7: IC2.1Y, ARDUINO_NANO.D5
  N8: IC2.2Y, ARDUINO_NANO.D4
  N9: IC2.3Y, ARDUINO_NANO.D3
  N10: IC2.4Y, ARDUINO_NANO.D6
  N11: IC2.5Y, ARDUINO_NANO.D7
  N12: DATA/POWER_pins.pin2, U2.DO/RI#5
  N13: DATA/POWER_pins.pin3, U2.DO/RI#6
  N14: TEST.anode, R5.Pin_1
  N15: DATA.anode, R2.Pin_1
  N16: ERROR.anode, R3.Pin_1
  N17: DONE.anode, R4.Pin_1
  N18: ARDUINO_NANO.D8, R5.Pin_0
  N19: ARDUINO_NANO.D9, R4.Pin_0
  N20: ARDUINO_NANO.D10, R3.Pin_0
  N21: ARDUINO_NANO.D11/MOSI, U2.DI
  N22: ARDUINO_NANO.D12/MISO, U2.RO
  N23: ARDUINO_NANO.A5, LCD_pins.pin1
  N24: ARDUINO_NANO.A4, LCD_pins.pin2
  N25: ARDUINO_NANO.D13/SCK, R2.Pin_0, U2.RE, U2.DE

notes:
  TSFRL_master_module_keys
  8) +5v
  7) keyUP
  6) keyRIGHT
  5) keyLEFT
  4) keyDOWN
  3)keySTART
  2)keySTOP/CANCEL
  1)GND
  SDA(LCD)
  SCL(LCD)
  GND
  keySTOP/CANCEL
  keySTART
  keyDOWN
  keyLEFT
  keyRIGHT
  keyUP
  VCC +5V
  CANCEL signal
  RS485_a
  RS485_b
  Test Stand For Radio Lamps, Test Stand For Radio Lamps project: master module, 1.0

custom parts:
  DS75176BN: RS-485 transceiver
